# Fritzing sketch rangkaian pemadam (saved by Fritzing 0.9.3b)

parts:
  M1 = DC Motor
  M2 = DC Motor
  IC2 = L293D [package=THT]
  J1 = Camdenboss CTB0158-9 [part_number=CTB0158-9 package=THT]
  Part1 = Arduino Uno (Rev3)
  VCC1 = Battery block 9V
  HC-SR04_Sensor_1 = HC-SR04 Ultrasonic Distance Sensor
  HC-SR04_Sensor_2 = HC-SR04 Ultrasonic Distance Sensor
  HC-SR04_Sensor_3 = HC-SR04 Ultrasonic Distance Sensor
  S1 = KY-026
  WATER_PUMP1 = water pump/motor  # not connected

nets:
  N1: M1.pin_1, IC2.Out_2_(_Controlled_by_Enable_1_)
  N2: M1.pin_2, IC2.Out_1_(_Controlled_by_Enable_1_)
  N3: M2.pin_1, IC2.Out_4_(_Controlled_by_Enable_2_)
  N4: M2.pin_2, IC2.Out_3_(_Controlled_by_Enable_2_)
  N5: IC2.Enable_1, J1.terminal_3, Part1.D10_PWM/SS
  N6: IC2.In_1, J1.terminal_4, Part1.D9_PWM
  N7: IC2.0V, J1.terminal_1, J1.terminal_2, VCC1.-
  N8: IC2.In_2, J1.terminal_5, Part1.D8
  N9: IC2.+Vmotor, IC2.+V, J1.terminal_9, VCC1.+
  N10: IC2.Enable_2, J1.terminal_8, Part1.D11_PWM/MOSI
  N11: IC2.In_3, J1.terminal_7, Part1.D7
  N12: IC2.In_4, J1.terminal_6, Part1.D6_PWM
  N13: Part1.A0, HC-SR04_Sensor_3.TRIG
  N14: Part1.A1, HC-SR04_Sensor_3.ECHO
  N15: Part1.A2, HC-SR04_Sensor_1.TRIG
  N16: Part1.A3, HC-SR04_Sensor_1.ECHO
  N17: Part1.A4/SDA, S1.pin1
  GND: Part1.GND, HC-SR04_Sensor_1.GND, HC-SR04_Sensor_2.GND, HC-SR04_Sensor_3.GND, S1.pin2
  N18: Part1.D2, HC-SR04_Sensor_2.ECHO
  N19: Part1.D3_PWM, HC-SR04_Sensor_2.TRIG
  VCC: Part1.5V, HC-SR04_Sensor_1.VCC, HC-SR04_Sensor_2.VCC, HC-SR04_Sensor_3.VCC, S1.pin3

notes:
  Servo bagian kiri mobil
  Servo bagian kanan mobil
  Servo bagian depan mobil
  Pompa Motor

custom parts:
  KY-026: ky-026 flame sensor module
  water pump/motor: WATER PUMP BY ARDUBLOCKTR
